# Fritzing sketch sensors (saved by Fritzing 0.9.2b)
breadboards: 1

parts:
  Part1 = Arduino Mega 2560 (Rev3)
  R1 = Resistor [tolerance=±5% resistance=10 package=THT]
  DHT1 = DHT22 Humidity and Temperature Sensor
  PIR1 = PIR sensor
  MIC1 = MAX4466 Electret Microphone Breakout Board
  LED1 = LED - 5mm [color="Red (633nm)" package="5 mm [THT]"]
  LED2 = LED - 5mm [color="Green (555nm)" package="5 mm [THT]"]
  LED3 = LED - 5mm [color="Blue (470nm)" package="5 mm [THT]"]
  R2 = Resistor [tolerance=±5% resistance=220 package=THT]
  R3 = Resistor [tolerance=±5% resistance=220 package=THT]
  R4 = Resistor [tolerance=±5% resistance=220 package=THT]

nets:
  N1: Part1.A0, MIC1.out
  N2: Part1.D13_PWM, R4.Pin_0
  N3: Part1.D9_PWM, R3.Pin_0
  N4: Part1.D8_PWM, R2.Pin_0
  VDD: Part1.5V, R1.Pin_1, DHT1.VDD, PIR1.VDD, MIC1.VCC
  GND: Part1.GND, DHT1.GND, PIR1.GND, MIC1.GND, LED1.cathode, LED2.cathode, LED3.cathode
  N5: Part1.D2_PWM, R1.Pin_0, DHT1.DATA
  N6: Part1.D3_PWM, PIR1.SIG
  N7: LED1.anode, R2.Pin_1
  N8: LED2.anode, R3.Pin_1
  N9: LED3.anode, R4.Pin_1

custom parts:
  MAX4466 Electret Microphone Breakout Board: MAX4466 Electrec Microphone Breakout Board
